# Fritzing sketch fritzing sketch (saved by Fritzing 0.9.3b)
breadboards: 1

parts:
  Part1 = Arduino Uno (Rev3) - ICSP
  green_led = LEDs [package=led10mm]
  R2 = Resistor [tolerance=±5% resistance=220 package="0603 [SMD]"]
  Red_led = LEDs [package=led10mm]
  U2 = ESP8266 WiFi Module [part_number=ESP8266]  # not connected
  U3 = FS1000A - 433Mhz RF Transmitter [package=THT]
  U4 = XD-RF-5V [package=THT]
  R3 = Resistor [tolerance=±5% resistance=220 package="0603 [SMD]"]

nets:
  N1: Part1.D12/MISO, R3.Pin_0
  N2: Part1.D13/SCK, R2.Pin_0
  GND: Part1.GND, green_led.A, Red_led.A, U3.GND, U4.GND
  N3: Part1.D3_PWM, U4.DATA
  N4: Part1.D7, U3.VCC
  5V: Part1.5V, U3.DATA, U4.VCC
  N5: green_led.C, R3.Pin_1
  N6: R2.Pin_1, Red_led.C

custom parts:
  ESP8266 WiFi Module: Generic WiFi Module based on the ESP8266 with onboard PCB antenna and UART communications
  FS1000A - 433Mhz RF Transmitter: This is 433Mhz RF transmitter with receiver kit for Arduino ARM MCU wireless Application environment: Remote control switch, receiver module, motorcycles, automobile anti-theft products, home security products, electric doors, shutter doors, windows, remote control socket, remote control LED, remote audio remote control electric doors, garage door remote control, remote control retractable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
  XD-RF-5V: This is 433Mhz RF transmitter with receiver kit for Arduino ARM MCU wireless Application environment: Remote control switch, receiver module, motorcycles, automobile anti-theft products, home security products, electric doors, shutter doors, windows, remote control socket, remote control LED, remote audio remote control electric doors, garage door remote control, remote control retractable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

// code stored in the sketch: arduino.ino
#include <RCSwitch.h>
#include <EEPROM.h>


RCSwitch mySwitch = RCSwitch();
int greenLed = 13;
int redLed = 12;
int transmitPin = 3; // Specify the pin for transmitting
int receivePin = 7; // Specify the pin for receiving
bool codesStored = false;
unsigned long receivedCode1, receivedCode2;
int eepromAddress1 = 0, eepromAddress2 = 4;


void writeLongToEEPROM(int address, unsigned long value) {
  byte four = (value & 0xFF);
  byte three = ((value >> 8) & 0xFF);
  byte two = ((value >> 16) & 0xFF);
  byte one = ((value >> 24) & 0xFF);


  EEPROM.write(address, four);
  EEPROM.write(address + 1, three);
  EEPROM.write(address + 2, two);
  EEPROM.write(address + 3, one);
}


unsigned long readLongFromEEPROM(int address) {
  unsigned long four = EEPROM.read(address);
  unsigned long three = EEPROM.read(address + 1);
  unsigned long two = EEPROM.read(address + 2);
  unsigned long one = EEPROM.read(address + 3);


  return ((four << 0) & 0xFF) + ((three << 8) & 0xFFFF) + ((two << 16) & 0xFFFFFF) + ((one << 24) & 0xFFFFFFFF);
}



void setup() {
  pinMode(greenLed, OUTPUT);
  pinMode(redLed, OUTPUT);
  mySwitch.enableTransmit(transmitPin);
  mySwitch.enableReceive(receivePin);
  Serial.begin(9600);


  // Check if codes are already stored in EEPROM
  if (EEPROM.read(eepromAddress1) != 0xFF && EEPROM.read(eepromAddress2) != 0xFF) {
    codesStored = true;
    digitalWrite(greenLed, HIGH);
    receivedCode1 = readLongFromEEPROM(eepromAddress1);
    receivedCode2 = readLongFromEEPROM(eepromAddress2);
  }
}


void loop() {
  if (codesStored) {
if (Serial.available()) {
      int command = Serial.read();
      if (command == '1') {
        mySwitch.send(receivedCode1); // Send "on" command
      } else if (command == '2') {
        mySwitch.send(receivedCode2); // Send "off" command
      }
    }
  } else {
    digitalWrite(redLed, HIGH);
    if (mySwitch.available()) {
      unsigned long value = mySwitch.getReceivedValue();
      if (value != 0) {
        Serial.print("Received RF code (On): ");
        Serial.println(value);
        receivedCode1 = value;
        writeLongToEEPROM(eepromAddress1, receivedCode1);
        digitalWrite(redLed, HIGH);
        delay(100);
        digitalWrite(redLed, LOW);
        delay(100);
        digitalWrite(redLed, HIGH);
        delay(100);
        digitalWrite(redLed, LOW);
        delay(100);
        if (mySwitch.available()) {
          unsigned long value2 = mySwitch.getReceivedValue();
          if (value2 != 0) {
            Serial.print("Received RF code (Off): ");
            Serial.println(value2);
            receivedCode2 = value2;
            writeLongToEEPROM(eepromAddress2, receivedCode2);
            digitalWrite(redLed, LOW);
            codesStored = true;
            digitalWrite(greenLed, HIGH);
        }
      }
    }
    }}  }
